# Fritzing sketch servo_connect (saved by Fritzing 0.9.3b)
breadboards: 1

parts:
  Raspberry_Pi_1 = Raspberry Pi 3 [part_number=RPI-3-V1.2]
  Font_5V = HLK-PM01
  R1 = Resistor [tolerance=±5% resistance=1k package=THT]
  J1 = Basic Servo

nets:
  GND: Raspberry_Pi_1.GND, Font_5V.-Vo, J1.gnd
  N1: Raspberry_Pi_1.GPIO18, R1.Pin_0
  N2: R1.Pin_1, J1.pulse
