# Fritzing sketch connexio_2 (saved by Fritzing 0.9.2b)
breadboards: 1

parts:
  CD4048B1 = CD4048B [part_number=CD4048B package="DIP (Dual Inline) [THT]"]
  Raspberry_Pi1 = Raspberry Pi 2
  U1 = GAS_SENSOR [package=mq-3]

nets:
  N1: CD4048B1.J, U1.A1
  N2: CD4048B1.Kc, Raspberry_Pi1.GND, U1.H1
  N3: CD4048B1.Ka, Raspberry_Pi1.GPIO8
  N4: CD4048B1.C, Raspberry_Pi1.GPIO9
  N5: CD4048B1.B, Raspberry_Pi1.GPIO11
  3V3: CD4048B1.EXPAND, CD4048B1.VDD, Raspberry_Pi1.3v3, Raspberry_Pi1.3V3, U1.H2
