# Fritzing sketch control_gpio (saved by Fritzing 0.9.3b)
breadboards: 1

parts:
  Raspberry_Pi_1 = Raspberry Pi 3 [part_number=RPI-3-V1.2]
  LED2 = LED - 3mm [color="Red (633nm)" package="3 mm [THT]"]
  LED3 = LED - 3mm [color="Yellow (585nm)" package="3 mm [THT]"]
  R1 = Resistor [tolerance=±5% resistance=220 package="0402 [SMD]"]
  R2 = Resistor [tolerance=±5% resistance=220 package="0402 [SMD]"]
  S1 = Pushbutton [package="[THT]"]

nets:
  N1: Raspberry_Pi_1.GND, LED2.cathode, LED3.cathode, S1.Pin_1, S1.Pin_2
  N2: Raspberry_Pi_1.GIPO24, S1.Pin_3, S1.Pin_4
  N3: Raspberry_Pi_1.GIPO23, R2.Pin_0
  N4: Raspberry_Pi_1.GIPO18, R1.Pin_0
  N5: LED2.anode, R1.Pin_1
  N6: LED3.anode, R2.Pin_1
